# Fritzing sketch AnalogSensorsAndVoltageDivider (saved by Fritzing 0.7.11b)
breadboards: 1

parts:
  Arduino2 = Arduino
  R7 = Resistor [tolerance=±5% resistance=10k package=THT]
  R8 = Rotary Potentiometer (Small) [maximum_resistance=100kΩ]
  R9 = Photocell (LDR) [package=THT]
  R10 = Resistor [tolerance=±5% resistance=10k package=THT]
  R11 = Basic Flex Resistor
  R12 = Resistor [tolerance=±5% resistance=10k package=THT]

nets:
  N1: Arduino2.+5V, R8.leg1, R9.pin_0, R11.pin_1
  N2: Arduino2.GND, R7.Pin_0, R10.Pin_0, R12.Pin_0
  N3: Arduino2.A0, R11.Pin_2, R12.Pin_1
  N4: Arduino2.A3, R9.pin_1, R10.Pin_1
  N5: Arduino2.A5, R8.wiper
  N6: R7.Pin_1, R8.leg2
