# Fritzing sketch LEDandFourButtons (saved by Fritzing 0.7.11b)
breadboards: 1

parts:
  LED1 = LED - 5mm [color="Red (633nm)" package="5 mm [THT]"]
  S1 = Pushbutton [package="[THT]"]
  S2 = Pushbutton [package="[THT]"]
  S3 = Pushbutton [package="[THT]"]
  S4 = Pushbutton [package="[THT]"]
  R3 = Resistor [tolerance=±5% resistance=10k package=THT]
  R2 = Resistor [tolerance=±5% resistance=10k package=THT]
  R1 = Resistor [tolerance=±5% resistance=10k package=THT]
  R5 = Resistor [tolerance=±5% resistance=10k package=THT]
  Arduino2 = Arduino

nets:
  N1: LED1.cathode, R3.Pin_1, R2.Pin_1, R1.Pin_1, R5.Pin_1, Arduino2.GND
  N2: LED1.anode, Arduino2.D13
  N3: S1.Pin_1, S1.Pin_2, R1.Pin_0, Arduino2.D7
  N4: S1.Pin_3, S1.Pin_4, S2.Pin_3, S2.Pin_4, S3.Pin_3, S3.Pin_4, S4.Pin_3, S4.Pin_4, Arduino2.+5V
  N5: S2.Pin_1, S2.Pin_2, R2.Pin_0, Arduino2.D6
  N6: S3.Pin_1, S3.Pin_2, R3.Pin_0, Arduino2.D5
  N7: S4.Pin_1, S4.Pin_2, R5.Pin_0, Arduino2.D4
