# Fritzing sketch BasicSpeakerCircuit (saved by Fritzing 0.7.11b)

parts:
  Arduino1 = Arduino
  R2 = Rotary Potentiometer (Small) [maximum_resistance=100kΩ]
  SPKR1 = Loudspeaker

nets:
  N1: Arduino1.GND, SPKR1.pin1
  N2: Arduino1.D13, R2.leg2
  N3: R2.wiper, SPKR1.pin2

notes:
  Potentiometer for volume control - try switching the digital pin to the left side and see what happens!
